// Logisim project 1bit_ALU.circ as structural Verilog: 1 circuit, main circuit one_bit_ALU
module one_bit_ALU (
  input  [3:0] ALU_Ctrl,
  input  A,
  input  B,
  input  Cin,
  output R,
  output Cout
);

  wire and_1_out, multiplexer_1_out, not_1_out, one_bit_adder_1_s, or_1_out, xor_1_out;

  not not_1 (not_1_out, B);
  Multiplexer #(.enable("false")) multiplexer_1 (.in0(B), .in1(not_1_out), .out(multiplexer_1_out), .sel(ALU_Ctrl[2]));
  and and_1 (and_1_out, A, multiplexer_1_out);
  or or_1 (or_1_out, A, multiplexer_1_out);
  xor xor_1 (xor_1_out, A, multiplexer_1_out);
  one_bit_adder one_bit_adder_1 (.A(A), .B(multiplexer_1_out), .Cin(Cin), .S(one_bit_adder_1_s), .Cout(Cout));
  Multiplexer #(.enable("false"), .select(2)) multiplexer_2 (
    .in0(and_1_out), .in1(or_1_out), .in2(xor_1_out), .in3(one_bit_adder_1_s), .out(R), .sel(ALU_Ctrl[1:0]));
endmodule
