// Logisim project ALU_32.circ as structural Verilog: 3 circuits, main circuit ALU4
module ALU4 (
  input  [3:0] ALU_Ctrl,
  input  [3:0] A,
  input  [3:0] B,
  input  Cin,
  output [3:0] R,
  output Cout
);

  wire one_bit_alu_1_cout, one_bit_alu_2_cout, one_bit_alu_3_cout;

  one_bit_ALU one_bit_alu_1 (.ALU_Ctrl(ALU_Ctrl), .A(A[0]), .B(B[0]), .Cin(Cin), .R(R[0]), .Cout(one_bit_alu_1_cout));
  one_bit_ALU one_bit_alu_2 (
    .ALU_Ctrl(ALU_Ctrl), .A(A[1]), .B(B[1]), .Cin(one_bit_alu_1_cout), .R(R[1]), .Cout(one_bit_alu_2_cout));
  one_bit_ALU one_bit_alu_3 (
    .ALU_Ctrl(ALU_Ctrl), .A(A[2]), .B(B[2]), .Cin(one_bit_alu_2_cout), .R(R[2]), .Cout(one_bit_alu_3_cout));
  one_bit_ALU one_bit_alu_4 (.ALU_Ctrl(ALU_Ctrl), .A(A[3]), .B(B[3]), .Cin(one_bit_alu_3_cout), .R(R[3]), .Cout(Cout));
endmodule

module ALU32 (
  input  [3:0] ALU_Ctrl,
  input  [31:0] A,
  input  [31:0] B,
  output [31:0] R,
  output Cout
);

  wire alu4_1_cout, alu4_2_cout, alu4_3_cout, alu4_4_cout, alu4_5_cout, alu4_6_cout, alu4_7_cout;

  ALU4 alu4_1 (.ALU_Ctrl(ALU_Ctrl), .A(A[3:0]), .B(B[3:0]), .Cin(ALU_Ctrl[2]), .R(R[3:0]), .Cout(alu4_1_cout));
  ALU4 alu4_2 (.ALU_Ctrl(ALU_Ctrl), .A(A[7:4]), .B(B[7:4]), .Cin(alu4_1_cout), .R(R[7:4]), .Cout(alu4_2_cout));
  ALU4 alu4_3 (.ALU_Ctrl(ALU_Ctrl), .A(A[11:8]), .B(B[11:8]), .Cin(alu4_2_cout), .R(R[11:8]), .Cout(alu4_3_cout));
  ALU4 alu4_4 (.ALU_Ctrl(ALU_Ctrl), .A(A[15:12]), .B(B[15:12]), .Cin(alu4_3_cout), .R(R[15:12]), .Cout(alu4_4_cout));
  ALU4 alu4_5 (.ALU_Ctrl(ALU_Ctrl), .A(A[19:16]), .B(B[19:16]), .Cin(alu4_4_cout), .R(R[19:16]), .Cout(alu4_5_cout));
  ALU4 alu4_6 (.ALU_Ctrl(ALU_Ctrl), .A(A[23:20]), .B(B[23:20]), .Cin(alu4_5_cout), .R(R[23:20]), .Cout(alu4_6_cout));
  ALU4 alu4_7 (.ALU_Ctrl(ALU_Ctrl), .A(A[27:24]), .B(B[27:24]), .Cin(alu4_6_cout), .R(R[27:24]), .Cout(alu4_7_cout));
  ALU4 alu4_8 (.ALU_Ctrl(ALU_Ctrl), .A(A[31:28]), .B(B[31:28]), .Cin(alu4_7_cout), .R(R[31:28]), .Cout(Cout));
endmodule

module ALU_CTRL (
  input  i6,
  input  i30,
  input  i14,
  input  i13,
  input  i12,
  input  i5,
  input  i4,
  output ALU_CTRL3,
  output ALU_CTRL2,
  output ALU_CTRL1,
  output ALU_CTRL0,
  output ALU_SRC
);

  wire xnor_1_out, xor_1_out;

  xnor xnor_1 (xnor_1_out, i13, i12);
  xor xor_1 (xor_1_out, i14, i6);
  nand nand_1 (ALU_CTRL1, i14, i13);
  nand nand_2 (ALU_CTRL0, xnor_1_out, xor_1_out);
  and and_1 (ALU_CTRL2, i30, i5, i4);
  nand nand_3 (ALU_SRC, i5, i4);

  assign ALU_CTRL3 = i6;
endmodule
