// Logisim project Lab3.circ as structural Verilog: 1 circuit, main circuit Datapath
module Datapath (
  input  [31:0] Instruction
);

  wire alu_ctrl_1_alu_src, clock_1_out;
  wire [3:0] alu_ctrl_1_alu_ctrl0;
  wire [31:0] alu32_1_r, bit_extender_1_out, multiplexer_1_out, reg_file_1_rdata1, reg_file_1_rdata2;

  Clock clock_1 (.out(clock_1_out));
  assign bit_extender_1_out = {{20{Instruction[31]}}, Instruction[31:20]};  // Bit_Extender bit_extender_1
  reg_file reg_file_1 (
    .RReg1(Instruction[19:15]), .RReg2(Instruction[24:20]), .Clock_in(clock_1_out), .WData(alu32_1_r),
    .Write(1'b1), .WReg(Instruction[11:7]), .RData1(reg_file_1_rdata1), .RData2(reg_file_1_rdata2));
  ALU_CTRL alu_ctrl_1 (
    .i6(Instruction[6]), .i30(Instruction[30]), .i14(Instruction[14]), .i13(Instruction[13]),
    .i12(Instruction[12]), .i5(Instruction[5]), .i4(Instruction[4]), .ALU_CTRL3(alu_ctrl_1_alu_ctrl0[3]),
    .ALU_CTRL2(alu_ctrl_1_alu_ctrl0[2]), .ALU_CTRL1(alu_ctrl_1_alu_ctrl0[1]),
    .ALU_CTRL0(alu_ctrl_1_alu_ctrl0[0]), .ALU_SRC(alu_ctrl_1_alu_src));
  Multiplexer #(.enable("false"), .width(32)) multiplexer_1 (
    .in0(reg_file_1_rdata2), .in1(bit_extender_1_out), .out(multiplexer_1_out), .sel(alu_ctrl_1_alu_src));
  ALU32 alu32_1 (
    .ALU_Ctrl(alu_ctrl_1_alu_ctrl0), .A(reg_file_1_rdata1), .B(multiplexer_1_out), .R(alu32_1_r));  // open: Cout
endmodule
