// Logisim project register_lib.circ as structural Verilog: 2 circuits, main circuit register_file_4_32
module register_file_4_32 (
  input  [1:0] Reg2,
  input  [1:0] Reg1,
  input  [31:0] WData,
  input  Clock_in,
  input  [1:0] WReg,
  input  Write,
  output [31:0] RData1,
  output [31:0] RData2
);

  wire demultiplexer_1_out0, demultiplexer_1_out1, demultiplexer_1_out2, demultiplexer_1_out3;
  wire [31:0] register_1_q, register_2_q, register_3_q, register_4_q;

  Demultiplexer #(.enable("false"), .select(2)) demultiplexer_1 (
    .out0(demultiplexer_1_out0), .out1(demultiplexer_1_out1), .out2(demultiplexer_1_out2),
    .out3(demultiplexer_1_out3), .in(Write), .sel(WReg));
  Register #(.width(32)) register_1 (
    .D(WData), .en(demultiplexer_1_out0), .clk(Clock_in), .Q(register_1_q));  // open: clr
  Register #(.width(32)) register_2 (
    .D(WData), .en(demultiplexer_1_out1), .clk(Clock_in), .Q(register_2_q));  // open: clr
  Register #(.width(32)) register_3 (
    .D(WData), .en(demultiplexer_1_out2), .clk(Clock_in), .Q(register_3_q));  // open: clr
  Register #(.width(32)) register_4 (
    .D(WData), .en(demultiplexer_1_out3), .clk(Clock_in), .Q(register_4_q));  // open: clr
  Multiplexer #(.enable("false"), .select(2), .width(32)) multiplexer_1 (
    .in0(register_1_q), .in1(register_2_q), .in2(register_3_q), .in3(register_4_q), .out(RData1), .sel(Reg1));
  Multiplexer #(.enable("false"), .select(2), .width(32)) multiplexer_2 (
    .in0(register_1_q), .in1(register_2_q), .in2(register_3_q), .in3(register_4_q), .out(RData2), .sel(Reg2));
endmodule

module reg_file (
  input  [4:0] RReg1,
  input  [4:0] RReg2,
  input  Clock_in,
  input  [31:0] WData,
  input  Write,
  input  [4:0] WReg,
  output [31:0] RData1,
  output [31:0] RData2
);

  wire W3_0, W7_4, W11_8, W15_12, W19_16, W23_20, W27_24, W31_28;
  wire [31:0] register_file_4_32_1_rdata1, register_file_4_32_1_rdata2, register_file_4_32_2_rdata1,
       register_file_4_32_2_rdata2, register_file_4_32_3_rdata1, register_file_4_32_3_rdata2,
       register_file_4_32_4_rdata1, register_file_4_32_4_rdata2, register_file_4_32_5_rdata1,
       register_file_4_32_5_rdata2, register_file_4_32_6_rdata1, register_file_4_32_6_rdata2,
       register_file_4_32_7_rdata1, register_file_4_32_7_rdata2, register_file_4_32_8_rdata1,
       register_file_4_32_8_rdata2;

  Demultiplexer #(.enable("false"), .select(3)) demultiplexer_1 (
    .out0(W3_0), .out1(W7_4), .out2(W11_8), .out3(W15_12), .out4(W19_16), .out5(W23_20), .out6(W27_24),
    .out7(W31_28), .in(Write), .sel(WReg[4:2]));
  register_file_4_32 register_file_4_32_1 (
    .Reg2(RReg2[1:0]), .Reg1(RReg1[1:0]), .WData(WData), .Clock_in(Clock_in), .WReg(WReg[1:0]), .Write(W3_0),
    .RData1(register_file_4_32_1_rdata1), .RData2(register_file_4_32_1_rdata2));
  register_file_4_32 register_file_4_32_2 (
    .Reg2(RReg2[1:0]), .Reg1(RReg1[1:0]), .WData(WData), .Clock_in(Clock_in), .WReg(WReg[1:0]), .Write(W7_4),
    .RData1(register_file_4_32_2_rdata1), .RData2(register_file_4_32_2_rdata2));
  register_file_4_32 register_file_4_32_3 (
    .Reg2(RReg2[1:0]), .Reg1(RReg1[1:0]), .WData(WData), .Clock_in(Clock_in), .WReg(WReg[1:0]),
    .Write(W11_8), .RData1(register_file_4_32_3_rdata1), .RData2(register_file_4_32_3_rdata2));
  register_file_4_32 register_file_4_32_4 (
    .Reg2(RReg2[1:0]), .Reg1(RReg1[1:0]), .WData(WData), .Clock_in(Clock_in), .WReg(WReg[1:0]),
    .Write(W15_12), .RData1(register_file_4_32_4_rdata1), .RData2(register_file_4_32_4_rdata2));
  register_file_4_32 register_file_4_32_5 (
    .Reg2(RReg2[1:0]), .Reg1(RReg1[1:0]), .WData(WData), .Clock_in(Clock_in), .WReg(WReg[1:0]),
    .Write(W19_16), .RData1(register_file_4_32_5_rdata1), .RData2(register_file_4_32_5_rdata2));
  register_file_4_32 register_file_4_32_6 (
    .Reg2(RReg2[1:0]), .Reg1(RReg1[1:0]), .WData(WData), .Clock_in(Clock_in), .WReg(WReg[1:0]),
    .Write(W23_20), .RData1(register_file_4_32_6_rdata1), .RData2(register_file_4_32_6_rdata2));
  register_file_4_32 register_file_4_32_7 (
    .Reg2(RReg2[1:0]), .Reg1(RReg1[1:0]), .WData(WData), .Clock_in(Clock_in), .WReg(WReg[1:0]),
    .Write(W27_24), .RData1(register_file_4_32_7_rdata1), .RData2(register_file_4_32_7_rdata2));
  register_file_4_32 register_file_4_32_8 (
    .Reg2(RReg2[1:0]), .Reg1(RReg1[1:0]), .WData(WData), .Clock_in(Clock_in), .WReg(WReg[1:0]),
    .Write(W31_28), .RData1(register_file_4_32_8_rdata1), .RData2(register_file_4_32_8_rdata2));
  Multiplexer #(.enable("false"), .select(3), .width(32)) multiplexer_1 (
    .in0(register_file_4_32_1_rdata1), .in1(register_file_4_32_2_rdata1), .in2(register_file_4_32_3_rdata1),
    .in3(register_file_4_32_4_rdata1), .in4(register_file_4_32_5_rdata1), .in5(register_file_4_32_6_rdata1),
    .in6(register_file_4_32_7_rdata1), .in7(register_file_4_32_8_rdata1), .out(RData1), .sel(RReg1[4:2]));
  Multiplexer #(.enable("false"), .select(3), .width(32)) multiplexer_2 (
    .in0(register_file_4_32_1_rdata2), .in1(register_file_4_32_2_rdata2), .in2(register_file_4_32_3_rdata2),
    .in3(register_file_4_32_4_rdata2), .in4(register_file_4_32_5_rdata2), .in5(register_file_4_32_6_rdata2),
    .in6(register_file_4_32_7_rdata2), .in7(register_file_4_32_8_rdata2), .out(RData2), .sel(RReg2[4:2]));
endmodule
