// Logisim project Lab4.circ as structural Verilog: 5 circuits, main circuit ImmGen
module ImmGen (
  input  [31:0] Instruction,
  output [31:0] IMM32
);

  Multiplexer #(.enable("false"), .select(2)) multiplexer_1 (
    .in0(Instruction[20]), .in1(Instruction[7]), .in3(1'b0), .out(IMM32[0]), .sel(Instruction[6:5]));  // open: in2
  Multiplexer #(.enable("false"), .width(4)) multiplexer_2 (
    .in0(Instruction[24:21]), .in1(Instruction[11:8]), .out(IMM32[4:1]), .sel(Instruction[5]));
  Multiplexer #(.enable("false")) multiplexer_3 (
    .in0(Instruction[7]), .in1(Instruction[31]), .out(IMM32[11]), .sel(Instruction[6]));
  assign IMM32[31:12] = {{19{Instruction[31]}}, Instruction[31]};  // Bit_Extender bit_extender_1

  assign IMM32[10:5] = Instruction[30:25];

  // Other names for the same wires on the sheet: I30_25[5:0] = Instruction[30:25]; I5 = Instruction[5];
  //   I6_5[1:0] = Instruction[6:5]; I6 = Instruction[6]; I7 = Instruction[7]; I11_8[3:0] = Instruction[11:8];
  //   I_20 = Instruction[20]; I24_21[3:0] = Instruction[24:21]; I31 = Instruction[31]
endmodule

module Control (
  input  [6:0] I6_0,
  output Branch,
  output MemRead,
  output MemtoReg,
  output RegWrite,
  output MemWrite
);

  wire nor_2_out, not_1_out;

  nor nor_1 (MemtoReg, I6_0[4], I6_0[3]);
  not not_1 (not_1_out, I6_0[5]);
  nor nor_2 (nor_2_out, I6_0[6], I6_0[4]);
  nor nor_3 (MemRead, I6_0[6], I6_0[5], I6_0[4]);
  or or_1 (RegWrite, not_1_out, I6_0[4]);
  and and_1 (MemWrite, nor_2_out, I6_0[5]);

  assign Branch = I6_0[6];
endmodule

module InstructionMemory (
  input  [23:0] Address,
  input  Clockin,
  output [31:0] Instruction
);

  wire not_1_out;

  not not_1 (not_1_out, Clockin);
  RAM #(.addrWidth(22), .asyncread("true"), .dataWidth(32)) ram_1 (
    .addr(Address[23:2]), .we(1'b0), .oe(not_1_out), .dout(Instruction));  // open: clk, din
endmodule

module DataMemory (
  input  [25:0] Address,
  input  MemWrite,
  input  MemRead,
  input  Clockin,
  input  [31:0] WriteData,
  output [31:0] ReadData
);

  RAM #(.addrWidth(24), .asyncread("true"), .dataWidth(32)) ram_1 (
    .addr(Address[25:2]), .we(MemWrite), .oe(MemRead), .clk(Clockin), .din(WriteData), .dout(ReadData));
endmodule

module Lab4 (
);

  wire alu_ctrl_1_alu_src, and_1_out, clock_1_out, comparator_1_eq, control_1_branch, control_1_memread,
       control_1_memtoreg, control_1_memwrite, control_1_regwrite;
  wire [3:0] alu_ctrl_1_alu_ctrl0;
  wire [7:0] register_1_q_2;
  wire [23:0] register_1_q;
  wire [31:0] adder_1_out, adder_2_out, alu32_1_r, datamemory_1_readdata, immgen_1_imm32,
       instructionmemory_1_instruction, multiplexer_1_out, multiplexer_2_out, multiplexer_3_out,
       reg_file_1_rdata1, reg_file_1_rdata2;

  Register #(.width(32)) register_1 (
    .D(multiplexer_2_out), .en(1'b1), .clk(clock_1_out), .Q({register_1_q_2, register_1_q}));  // open: clr
  Clock clock_1 (.out(clock_1_out));
  Adder #(.width(32)) adder_1 (.a({register_1_q_2, register_1_q}), .b(32'h4), .out(adder_1_out));  // open: cin, cout
  InstructionMemory instructionmemory_1 (
    .Address(register_1_q), .Clockin(clock_1_out), .Instruction(instructionmemory_1_instruction));
  ImmGen immgen_1 (.Instruction(instructionmemory_1_instruction), .IMM32(immgen_1_imm32));
  Control control_1 (
    .I6_0(instructionmemory_1_instruction[6:0]), .Branch(control_1_branch), .MemRead(control_1_memread),
    .MemtoReg(control_1_memtoreg), .RegWrite(control_1_regwrite), .MemWrite(control_1_memwrite));
  reg_file reg_file_1 (
    .RReg1(instructionmemory_1_instruction[19:15]), .RReg2(instructionmemory_1_instruction[24:20]),
    .Clock_in(clock_1_out), .WData(multiplexer_3_out), .Write(control_1_regwrite),
    .WReg(instructionmemory_1_instruction[11:7]), .RData1(reg_file_1_rdata1), .RData2(reg_file_1_rdata2));
  ALU_CTRL alu_ctrl_1 (
    .i6(instructionmemory_1_instruction[6]), .i30(instructionmemory_1_instruction[30]),
    .i14(instructionmemory_1_instruction[14]), .i13(instructionmemory_1_instruction[13]),
    .i12(instructionmemory_1_instruction[12]), .i5(instructionmemory_1_instruction[5]),
    .i4(instructionmemory_1_instruction[4]), .ALU_CTRL3(alu_ctrl_1_alu_ctrl0[3]),
    .ALU_CTRL2(alu_ctrl_1_alu_ctrl0[2]), .ALU_CTRL1(alu_ctrl_1_alu_ctrl0[1]),
    .ALU_CTRL0(alu_ctrl_1_alu_ctrl0[0]), .ALU_SRC(alu_ctrl_1_alu_src));
  Multiplexer #(.enable("false"), .width(32)) multiplexer_1 (
    .in0(reg_file_1_rdata2), .in1(immgen_1_imm32), .out(multiplexer_1_out), .sel(alu_ctrl_1_alu_src));
  Comparator #(.width(32)) comparator_1 (
    .a(reg_file_1_rdata1), .b(reg_file_1_rdata2), .eq(comparator_1_eq));  // open: gt, lt
  ALU32 alu32_1 (
    .ALU_Ctrl(alu_ctrl_1_alu_ctrl0), .A(reg_file_1_rdata1), .B(multiplexer_1_out), .R(alu32_1_r));  // open: Cout
  Adder #(.width(32)) adder_2 (
    .a({register_1_q_2, register_1_q}), .b(immgen_1_imm32), .out(adder_2_out));  // open: cin, cout
  and and_1 (and_1_out, control_1_branch, comparator_1_eq);
  Multiplexer #(.enable("false"), .width(32)) multiplexer_2 (
    .in0(adder_1_out), .in1(adder_2_out), .out(multiplexer_2_out), .sel(and_1_out));
  DataMemory datamemory_1 (
    .Address(alu32_1_r[25:0]), .MemWrite(control_1_memwrite), .MemRead(control_1_memread),
    .Clockin(clock_1_out), .WriteData(reg_file_1_rdata2), .ReadData(datamemory_1_readdata));
  Multiplexer #(.enable("false"), .width(32)) multiplexer_3 (
    .in0(alu32_1_r), .in1(datamemory_1_readdata), .out(multiplexer_3_out), .sel(control_1_memtoreg));
endmodule
